// Logisim project TME1.circ as structural Verilog
module mon_xor (
  input  a,
  input  b,
  input  b_2,
  input  a_2,
  output f
);

  wire and_1_out, and_2_out, not_1_out, not_2_out, or_1_out;

  not not_1 (not_1_out, b);
  not not_2 (not_2_out, a_2);
  and and_1 (and_1_out, a, not_1_out);
  and and_2 (and_2_out, b_2, not_2_out);
  or or_1 (or_1_out, and_1_out, and_2_out);
endmodule

module mux2 (
  input  i,
  input  e0,
  input  e1,
  output y
);

  wire and_1_out, and_2_out, not_1_out;

  not not_1 (not_1_out, i);
  and and_1 (and_1_out, not_1_out, e0);
  and and_2 (and_2_out, i, e1);
  or or_1 (y, and_1_out, and_2_out);
endmodule

module mux2_4bits (
  input  a0,
  input  b0,
  input  a1,
  input  b1,
  input  a2,
  input  b2,
  input  a3,
  input  b3,
  input  i,
  output s0,
  output s1,
  output s2,
  output s3
);

  mux2 mux2_1 (.i(a0), .e0(b0), .y(b0), .e1(i));
  mux2 mux2_2 (.i(a1), .e0(b1), .y(s1), .e1(i));
  mux2 mux2_3 (.i(a2), .e0(b2), .y(b2), .e1(i));
  mux2 mux2_4 (.i(a3), .e0(b3), .y(s3), .e1(i));

  assign s0 = b0;
  assign s2 = b2;
endmodule

module mux4_1bit (
  input  e0,
  input  e1,
  input  i0,
  input  e2,
  input  e3,
  input  i1,
  output s
);

  wire not_1_out, not_2_out;

  not not_1 (not_1_out, i0);
  not not_2 (not_2_out, i1);
  mux2 mux2_1 (.i(e0), .e0(not_1_out), .e1(i0));  // open: y
  mux2 mux2_2 (.i(e2), .e0(not_2_out), .e1(i1));  // open: y
  mux2 mux2_3 (.i(not_1_out), .y(s), .e1(not_2_out));  // open: e0

  assign e1 = e0;
  assign e3 = e2;
endmodule

module ex5 (
  input  i0,
  input  e0,
  input  e1,
  input  e2,
  input  e3,
  input  i1,
  input  e4,
  input  e5,
  input  e6,
  input  e7,
  output s
);

  wire mux2_1_y, mux2_2_y, mux2_3_y;

  mux2 mux2_1 (.i(e0), .e0(i0), .y(mux2_1_y));  // open: e1
  mux2 mux2_2 (.e0(e2), .y(mux2_2_y), .e1(i0));  // open: i
  mux2 mux2_3 (.i(i0), .e0(e4), .y(mux2_3_y));  // open: e1
  mux2 mux2_4 (.i(e6), .e0(e6), .y(e6), .e1(e6));
  mux2 mux2_5 (.i(mux2_1_y), .e0(i1), .e1(mux2_2_y));  // open: y
  mux2 mux2_6 (.i(i1), .e0(mux2_3_y), .y(i1), .e1(e6));
  mux2 mux2_7 (.i(i1));  // open: e0, y, e1

  assign e1 = e0;
  assign e3 = e2;
  assign e5 = e4;
  assign e7 = e6;
  assign s = i1;
endmodule

module mux8 (
  input  i0,
  input  e0,
  input  e1,
  input  e2,
  input  e3,
  input  i1,
  input  e4,
  input  e5,
  input  e6,
  input  e7,
  output s
);

  wire undriven, undriven_2, undriven_3;

  mux2 mux2_1 (.i(e0), .e0(i0), .e1(undriven));  // open: y
  mux2 mux2_2 (.i(undriven), .e0(e2), .e1(i0));  // open: y
  mux2 mux2_3 (.e0(e4), .e1(undriven_2));  // open: i, y
  mux2 mux2_4 (.i(undriven_2), .e0(e6), .e1(i0));  // open: y
  mux2 mux2_5 (.i(undriven), .e0(i1));  // open: y, e1
  mux2 mux2_6 (.i(i1), .e0(undriven_3), .e1(undriven_2));  // open: y
  mux2 mux2_7 (.i(i1), .e0(s), .e1(undriven_3));  // open: y

  assign e1 = e0;
  assign e3 = e2;
  assign e5 = e4;
  assign e7 = e6;
endmodule
