// Logisim project TME2.circ as structural Verilog
module add_1bit (
  input  A,
  input  B,
  input  Cin,
  output S,
  output Cout
);

  wire and_1_out, and_2_out, xor_1_out, xor_2_out;

  xor xor_1 (xor_1_out, Cin, B);
  xor xor_2 (xor_2_out, Cin, B);
  and and_1 (and_1_out, Cin, B);
  and and_2 (and_2_out, xor_2_out, A);
  xor xor_3 (S, xor_1_out, A);
  or or_1 (Cout, and_2_out, and_1_out);
endmodule

module add_4bits (
  input  A0,
  input  B0,
  input  A1,
  input  B1,
  input  A2,
  input  B2,
  input  A3,
  input  B3,
  input  Cin,
  output Cout,
  output S
);

  wire add_1bit_1_cout, add_1bit_1_s, add_1bit_2_cout, add_1bit_2_s, add_1bit_3_cout, add_1bit_3_s,
       add_1bit_4_s;

  add_1bit add_1bit_1 (.A(B0), .B(A0), .Cin(Cin), .S(add_1bit_1_s), .Cout(add_1bit_1_cout));
  add_1bit add_1bit_2 (.A(B1), .B(A1), .Cin(add_1bit_1_cout), .S(add_1bit_2_s), .Cout(add_1bit_2_cout));
  add_1bit add_1bit_3 (.A(B2), .B(A2), .Cin(add_1bit_2_cout), .S(add_1bit_3_s), .Cout(add_1bit_3_cout));
  add_1bit add_1bit_4 (.A(B3), .B(A3), .Cin(add_1bit_3_cout), .S(add_1bit_4_s), .Cout(Cout));
  or or_1 (S, add_1bit_4_s, add_1bit_3_s, add_1bit_2_s, add_1bit_1_s);
endmodule

module ALUv1 (
  input  a0,
  input  a1,
  input  a2,
  input  a3,
  input  Cin,
  input  Aluop,
  input  b0,
  input  b1,
  input  b2,
  input  b3,
  output S0,
  output S1,
  output S2,
  output S3,
  output Cout
);

  wire add_1bit_1_s, add_1bit_2_cout, add_1bit_2_s, add_1bit_3_cout, add_1bit_3_s, add_1bit_4_cout,
       add_1bit_4_s, add_1bit_5_cout, add_1bit_6_cout, add_1bit_7_cout, and_1_out, multiplexer_1_out,
       multiplexer_2_out, multiplexer_3_out, multiplexer_4_out, not_1_out, not_2_out, not_3_out, not_4_out;

  not not_1 (not_1_out, b0);
  not not_2 (not_2_out, b1);
  not not_3 (not_3_out, b2);
  not not_4 (not_4_out, b3);
  Multiplexer multiplexer_1 (.in0(b0), .in1(not_1_out), .out(multiplexer_1_out), .sel(Aluop));  // open: en
  Multiplexer multiplexer_2 (.in0(b1), .in1(not_2_out), .out(multiplexer_2_out), .sel(Aluop));  // open: en
  Multiplexer multiplexer_3 (.in0(b2), .in1(not_3_out), .out(multiplexer_3_out), .sel(Aluop));  // open: en
  Multiplexer multiplexer_4 (.in0(b3), .in1(not_4_out), .out(multiplexer_4_out), .sel(Aluop));  // open: en
  add_1bit add_1bit_1 (.A(multiplexer_4_out), .B(1'b0), .Cin(add_1bit_3_cout), .S(add_1bit_1_s));  // open: Cout
  and and_1 (and_1_out, Aluop, 1'b1);
  add_1bit add_1bit_2 (
    .A(multiplexer_2_out), .B(1'b0), .Cin(add_1bit_4_cout), .S(add_1bit_2_s), .Cout(add_1bit_2_cout));
  add_1bit add_1bit_3 (
    .A(multiplexer_3_out), .B(1'b0), .Cin(add_1bit_2_cout), .S(add_1bit_3_s), .Cout(add_1bit_3_cout));
  add_1bit add_1bit_4 (.A(multiplexer_1_out), .B(and_1_out), .Cin(1'b0), .S(add_1bit_4_s), .Cout(add_1bit_4_cout));
  add_1bit add_1bit_5 (.A(a0), .B(add_1bit_4_s), .Cin(Cin), .S(S0), .Cout(add_1bit_5_cout));
  add_1bit add_1bit_6 (.A(a1), .B(add_1bit_2_s), .Cin(add_1bit_5_cout), .S(S1), .Cout(add_1bit_6_cout));
  add_1bit add_1bit_7 (.A(a2), .B(add_1bit_3_s), .Cin(add_1bit_6_cout), .S(S2), .Cout(add_1bit_7_cout));
  add_1bit add_1bit_8 (.A(a3), .B(add_1bit_1_s), .Cin(add_1bit_7_cout), .S(S3), .Cout(Cout));
endmodule

module ALUv2 (
  input  a0,
  input  a1,
  input  a2,
  input  a3,
  input  Cin,
  input  Aluop,
  input  b0,
  input  b1,
  input  b2,
  input  b3,
  output ZF,
  output S0,
  output S1,
  output S2,
  output SF,
  output S3,
  output CF,
  output OV
);

  wire add_1bit_1_s, add_1bit_2_cout, add_1bit_2_s, add_1bit_3_cout, add_1bit_3_s, add_1bit_4_cout,
       add_1bit_4_s, add_1bit_5_cout, add_1bit_6_cout, add_1bit_7_cout, and_1_out, multiplexer_1_out,
       multiplexer_2_out, multiplexer_3_out, multiplexer_4_out, not_1_out, not_2_out, not_3_out, not_4_out;

  not not_1 (not_1_out, b0);
  not not_2 (not_2_out, b1);
  not not_3 (not_3_out, b2);
  not not_4 (not_4_out, b3);
  Multiplexer multiplexer_1 (.in0(b0), .in1(not_1_out), .out(multiplexer_1_out), .sel(Aluop));  // open: en
  Multiplexer multiplexer_2 (.in0(b1), .in1(not_2_out), .out(multiplexer_2_out), .sel(Aluop));  // open: en
  Multiplexer multiplexer_3 (.in0(b2), .in1(not_3_out), .out(multiplexer_3_out), .sel(Aluop));  // open: en
  Multiplexer multiplexer_4 (.in0(b3), .in1(not_4_out), .out(multiplexer_4_out), .sel(Aluop));  // open: en
  add_1bit add_1bit_1 (.A(multiplexer_4_out), .B(1'b0), .Cin(add_1bit_3_cout), .S(add_1bit_1_s));  // open: Cout
  and and_1 (and_1_out, Aluop, 1'b1);
  add_1bit add_1bit_2 (
    .A(multiplexer_2_out), .B(1'b0), .Cin(add_1bit_4_cout), .S(add_1bit_2_s), .Cout(add_1bit_2_cout));
  add_1bit add_1bit_3 (
    .A(multiplexer_3_out), .B(1'b0), .Cin(add_1bit_2_cout), .S(add_1bit_3_s), .Cout(add_1bit_3_cout));
  add_1bit add_1bit_4 (.A(multiplexer_1_out), .B(and_1_out), .Cin(1'b0), .S(add_1bit_4_s), .Cout(add_1bit_4_cout));
  add_1bit add_1bit_5 (.A(a0), .B(add_1bit_4_s), .Cin(Cin), .S(S0), .Cout(add_1bit_5_cout));
  add_1bit add_1bit_6 (.A(a1), .B(add_1bit_2_s), .Cin(add_1bit_5_cout), .S(S1), .Cout(add_1bit_6_cout));
  add_1bit add_1bit_7 (.A(a2), .B(add_1bit_3_s), .Cin(add_1bit_6_cout), .S(S2), .Cout(add_1bit_7_cout));
  add_1bit add_1bit_8 (.A(a3), .B(add_1bit_1_s), .Cin(add_1bit_7_cout), .S(S3), .Cout(CF));
  xor xor_1 (OV, CF, add_1bit_7_cout);
  nor nor_1 (ZF, S3, S2, S1, S0);

  assign SF = S3;
endmodule
